# Fritzing sketch led tester (saved by Fritzing 0.9.2b)

parts:
  C1 = Electrolytic Capacitor [capacitance=0.1mF package="100 mil [THT, electrolytic]"]  # not connected
  R1 = Resistor [tolerance=±5% resistance=470 package=THT]  # not connected
  R2 = Resistor [tolerance=±5% resistance=4.7k package=THT]  # not connected
  Part1 = Arduino Pro Mini v13
  LCD1 = LCD screen
  LCM1602_IIC2 = LCM1602 IIC [part_number="LCM1602 IIC" chip_label="LCM1602 IIC" package="DIP (Dual Inline) [THT]"]
  Power_plug2 = Power plug
  NEOPIXEL2 = Neopixel Strip -- White (30/m)
  proto1 = Adafruit_PermaProto_1_4_Board
  S3 = Pushbutton [package=THT]  # not connected
  U1 = POT [package=alps_pot]  # not connected

nets:
  N1: Part1.A4, LCM1602_IIC2.SDA
  N2: Part1.A5, LCM1602_IIC2.SCL
  N3: Part1.RAW, proto1.connectorY12
  N4: Part1.GND, proto1.connectorZ13
  N5: Part1.VCC, proto1.connectorW1
  N6: Part1.A0, proto1.connectorC3
  N7: Part1.D13/SCK, proto1.connectorD9
  N8: Part1.D6_PWM, proto1.connectorA10
  VSS: LCD1.VSS, LCM1602_IIC2.VSS
  VDD: LCD1.VDD, LCM1602_IIC2.VDD
  N9: LCD1.V0, LCM1602_IIC2.V0
  N10: LCD1.RS, LCM1602_IIC2.RS
  N11: LCD1.R/W, LCM1602_IIC2.RW
  N12: LCD1.E, LCM1602_IIC2.E
  N13: LCD1.DB0, LCM1602_IIC2.D0
  N14: LCD1.DB1, LCM1602_IIC2.D1
  N15: LCD1.DB2, LCM1602_IIC2.D2
  N16: LCD1.DB3, LCM1602_IIC2.D3
  N17: LCD1.DB4, LCM1602_IIC2.D4
  N18: LCD1.DB5, LCM1602_IIC2.D5
  N19: LCD1.DB6, LCM1602_IIC2.D6
  N20: LCD1.DB7, LCM1602_IIC2.D7
  N21: LCD1.LED+, LCM1602_IIC2.A
  N22: LCD1.LED-, LCM1602_IIC2.K
  N23: LCM1602_IIC2.GND, proto1.connectorZ10
  N24: LCM1602_IIC2.VCC, proto1.connectorY11
  N25: Power_plug2.VCC, proto1.connectorY15
  N26: Power_plug2.GND, proto1.connectorZ15
  N27: NEOPIXEL2.GND, proto1.connectorZ1
  N28: NEOPIXEL2.Din, proto1.connectorI10
  N29: NEOPIXEL2.+5V, proto1.connectorY1
  N30: proto1.connectorA2, proto1.connectorW2
  N31: proto1.connectorA4, proto1.connectorX4
  N32: proto1.connectorA6, proto1.connectorW6
  N33: proto1.connectorX14, proto1.connectorZ14

custom parts:
  LCM1602 IIC: I2C-Module to use a 1602 or 2004 LCD on with the wire.h libory Serial LCD Modul
  Neopixel Strip -- White (30/m): These NeoPixel strips have 30 digitally-addressable pixel LEDs per meter and are very affordable and are only 12.5 mm wide, 10 mm if you remove the strip from the casing.
